# Fritzing sketch HX_Stomp_Midi (saved by Fritzing 0.9.3b)
circuit board: 8.46667cm x 5.64444cm
breadboards: 1

parts:
  Bauteil1 = Arduino Pro Mini (5V)
  U1 = MIDI_CONN_FEMALE [package=din_5_female]
  Bauteil2 = ws2812b [package="smd 2812b"]
  J5 = Power Jack [package=power_jack_slot]
  C1 = Capacitor [part_number="0.1 µF" package=cap-pth-small2]
  R1 = Resistor [tolerance=±1% resistance=220 package="1206 [SMD]"]
  R2 = Resistor [tolerance=±1% resistance=220 package="1206 [SMD]"]
  D1 = Zener Diode [part_number=1N4148 breakdown_voltage=3.6V package="300 mil [THT]"]
  S3 = Pushbutton [package="[THT]"]
  S2 = Pushbutton [package="[THT]"]
  S1 = Pushbutton [package="[THT]"]

nets:
  N1: Bauteil1.TXO, R1.Pin_1
  GND: Bauteil1.GND, Bauteil2.VSS, J5.GND, C1.1, S3.Pin_1, S3.Pin_2, S2.Pin_1, S2.Pin_2, S1.Pin_1, S1.Pin_2
  N2: Bauteil1.RAW, D1.cathode
  VCC: Bauteil1.VCC, Bauteil2.VDD, C1.2
  N3: Bauteil1.MISO, S3.Pin_3, S3.Pin_4
  N4: Bauteil1.MOSI, S2.Pin_3, S2.Pin_4
  N5: Bauteil1.D10, S1.Pin_3, S1.Pin_4
  N6: Bauteil1.D9, U1.NC1
  N7: Bauteil1.D8, R2.Pin_1
  N8: Bauteil1.D4, Bauteil2.DIN
  N9: U1.MIDI_IN, R2.Pin_0
  N10: U1.MIDI_OUT, R1.Pin_0
  N11: J5.PWR, D1.anode
